# Fritzing sketch ProTinket Volume Knob Fritzing (saved by Fritzing 0.9.1b)
breadboards: 1

parts:
  ENCODER1 = Rotary Encoder with Knob

nets:
  N1: ENCODER1.no_name_yet#1, ENCODER1.no_name_yet#2

custom parts:
  Rotary Encoder with Knob: Rotary Encoder with 1/4" Shaft and Knob
